# Fritzing sketch LAB5_Fritzing0 (saved by Fritzing 1.0.4)
circuit board: 8.46667cm x 5.64444cm
breadboards: 1

parts:
  M1 = FireBeetle ESP32-E
  LED1 = LED - 5mm [color="Red (633nm)" current=0.030A package="5 mm [THT]"]
  DHT11_1 = DHT11 module

nets:
  N1: M1.pin_12, M1.pin_20, LED1.anode, DHT11_1.GND
  N2: M1.pin_13, DHT11_1.VCC
  N3: M1.pin_22, DHT11_1.DATA
  N4: M1.pin_28, LED1.cathode

custom parts:
  FireBeetle ESP32-E: FireBeetle ESP32-E, specially designed for IoT, is an ESP-WROOM-32E-based main controller board with dual-core chips. It supports WiFi and Bluetooth dual-mode communication and features a small size, ultra-low power consumption, on-board charging circuit, and easy-to-use interface, which can be conveniently used for smart home IoT, industrial IoT applications, wearable devices, and so on. You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
  DHT11 module: DHT11 black pcb module
